# Fritzing sketch HolaMundo_DIP (saved by Fritzing 0.9.9b)
breadboards: 1

parts:
  U1 = atmega328 [package=dip]  # not connected
  USBTTL1 = USB TTL Serial Cable
  LED1 = smd LED [color="Red (633nm)" package="1206 [SMD]"]
  R1 = Resistor [tolerance=±5% resistance=330 power=0.25 package=THT]

nets:
  N1: USBTTL1.GND, R1.Pin_0
  N2: LED1.cathode, R1.Pin_1

notes:
  28
  7
  8
  13
  1
  Hola Mundo
  Note:
  AVR (pin)
  +5V (7)
  GND (8,22)
  PB6 (19)
  19
  22
  JDGC
  atmega328p
  Withot Arduino Bootloader
  DIP package
