# Fritzing sketch HolaMundo_Nano (saved by Fritzing 0.9.9b)
breadboards: 1

parts:
  LED1 = LED - 5mm [color="Red (633nm)" current=0.030 package="5 mm [THT]"]
  R2 = Resistor [tolerance=±5% power=0.25 resistance=330 package=THT]
  Componente1 = Arduino Nano (Rev3.0)

nets:
  N1: LED1.cathode, R2.Pin_1
  N2: LED1.anode, Componente1.D13/SCK
  N3: R2.Pin_0, Componente1.GND

notes:
  Hola Mundo
