# Fritzing sketch HolaMundo_Uno (saved by Fritzing 0.9.9b)
breadboards: 1

parts:
  LED1 = LED - 5mm [color="Red (633nm)" current=0.030 package="5 mm [THT]"]
  R2 = Resistor [tolerance=±5% power=0.25 resistance=330 package=THT]
  Componente2 = Arduino Uno (Rev3) - ICSP

nets:
  N1: LED1.cathode, R2.Pin_1
  N2: LED1.anode, Componente2.D13/SCK
  N3: R2.Pin_0, Componente2.GND

notes:
  JDGC
  Arduino Uno  Development Board
  Hola Mundo
  DIP  package
  atmega328p
